# Fritzing sketch spica (saved by Fritzing 0.9.3b)
circuit board: 12.6845cm x 5.81377cm
breadboards: 1

parts:
  U1 = ESP32S-HiLetgo [part_number=ESP32S-HiLetgo]
  IC1 = V_REG_LD1117VXX [package=78xxl]
  C1 = Ceramic Capacitor [capacitance=0.1µF voltage=6.3V package="100 mil [THT, multilayer]"]
  C2 = Electrolytic Capacitor [capacitance=100µF package="100 mil [THT, electrolytic]"]
  C3 = Electrolytic Capacitor [capacitance=1mF voltage=10V package="100 mil [THT, electrolytic]"]
  IC2 = AE-DRV8835-S [package="DIP (Dual Inline) [THT]"]
  VCC2 = 4 x AAA Battery Mount
  R1 = Resistor [tolerance=±5% resistance=220 package=THT]
  M1 = DC Motor
  M2 = DC Motor
  R2 = Trimmer Potentiometer [maximum_resistance=10kΩ package=THT]

nets (from the schematic view):
  N1: U1.3.3, IC1.OUT, C2.+, IC2.MODE, IC2.VCC
  N2: U1.GPIO34, R2.leg1
  N3: U1.GPIO32, R2.leg2
  N4: U1.GPIO33, R2.wiper
  N5: U1.GPIO25, IC2.AIN1
  N6: U1.GPIO26, IC2.AIN2
  GND: U1.GND, IC1.GND, C1.0, C2.-, C3.-, IC2.GND, VCC2.-
  N7: U1.GPIO16, IC2.BIN1
  N8: U1.GPIO17, IC2.BIN2
  N9: IC1.IN, C1.1, C3.+, R1.Pin_1
  N10: IC2.VM, VCC2.+, R1.Pin_0
  N11: IC2.AOUT1, M1.pin_1
  N12: IC2.AOUT2, M1.pin_2
  N13: IC2.BOUT1, M2.pin_1
  N14: IC2.BOUT2, M2.pin_2

custom parts:
  ESP32S-HiLetgo: HiLetgo ESP-WROOM-32 ESP32 ESP-32S Development Board 2.4GHz Dual-Mode WiFi + Bluetooth Dual Cores Microcontroller The ESP32 integrated with Antenna switches, RF Balun, power amplifiers, low-noise amplifiers, filters, and management modules, and the entire solution occupies the least area of PCB. 2.4 GHz Wi-Fi plus Bluetooth dual-mode chip, with TSMC Ultra-low power consumption 40nm technology,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
  AE-DRV8835-S: A DRV8835 breakout board by Akizuki Denshi Tsusho Co.,Ltd.
